# Fritzing sketch onDockingStation (saved by Fritzing 0.8.5b)
breadboards: 1

parts:
  Part1 = Arduino Uno (Rev3)
  IR_Emitter = LEDs [package=led10mm]
  R2 = Resistor [tolerance=±5% resistance=330 package=THT]

nets:
  N1: Part1.D3_PWM, R2.Pin_0
  N2: Part1.GND, IR_Emitter.C
