# Fritzing sketch onRobot (saved by Fritzing 0.8.5b)
breadboards: 1

parts:
  Part1 = Arduino Uno (Rev3)
  IR1 = TSOP312.., 314.. [package=THT]
  IR2 = TSOP312.., 314.. [package=THT]

nets:
  N1: Part1.D2, IR1.Data
  N2: Part1.D3_PWM, IR2.Data
  GND: Part1.GND, IR1.GND, IR2.GND
  N3: IR1.Vs, IR2.Vs
